// Logisim project computer_made_with_logisim.circ as structural Verilog
// cNot
module \not  (
  input  in_1,
  output out_2
);

  nand nand_1 (out_2, in_1, in_1);
endmodule

// cAnd
module \and  (
  input  in_1,
  input  in_2,
  output out_3
);

  wire nand_1_out;

  nand nand_1 (nand_1_out, in_1, in_2);
  \not  not_1 (.in_1(nand_1_out), .out_2(out_3));
endmodule

// cOr
module \or  (
  input  in_1,
  input  in_2,
  output out_3
);

  wire not_1_out_2, not_2_out_2;

  \not  not_1 (.in_1(in_1), .out_2(not_1_out_2));
  \not  not_2 (.in_1(in_2), .out_2(not_2_out_2));
  nand nand_1 (out_3, not_1_out_2, not_2_out_2);
endmodule

// cXor
module \xor  (
  input  in_1,
  input  in_2,
  output out_3
);

  wire and_1_out_3, and_2_out_3, not_1_out_2, not_2_out_2;

  \and  and_1 (.in_1(in_1), .in_2(not_1_out_2), .out_3(and_1_out_3));
  \not  not_1 (.in_1(in_2), .out_2(not_1_out_2));
  \not  not_2 (.in_1(in_1), .out_2(not_2_out_2));
  \and  and_2 (.in_1(not_2_out_2), .in_2(in_2), .out_3(and_2_out_3));
  \or  or_1 (.in_1(and_1_out_3), .in_2(and_2_out_3), .out_3(out_3));
endmodule

module or8way (
  input  [7:0] in_1,
  output out_2
);

  wire or_1_out, or_2_out, or_3_out, or_4_out, or_5_out, or_6_out;

  or or_1 (or_1_out, in_1[0], in_1[1]);
  or or_2 (or_2_out, or_1_out, in_1[2]);
  or or_3 (or_3_out, or_2_out, in_1[3]);
  or or_4 (or_4_out, or_3_out, in_1[4]);
  or or_5 (or_5_out, or_4_out, in_1[5]);
  or or_6 (or_6_out, or_5_out, in_1[6]);
  or or_7 (out_2, or_6_out, in_1[7]);
endmodule

module or16way (
  input  [15:0] in_1,
  output out_2
);

  wire or8way_1_out_2, or8way_2_out_2;

  or8way or8way_1 (.in_1(in_1[7:0]), .out_2(or8way_1_out_2));
  or8way or8way_2 (.in_1(in_1[15:8]), .out_2(or8way_2_out_2));
  or or_1 (out_2, or8way_1_out_2, or8way_2_out_2);
endmodule

// cAnd16
module and16 (
  input  [15:0] in_1,
  input  [15:0] in_2,
  output [15:0] out_3
);

  and and_1 (out_3[0], in_1[0], in_2[0]);
  and and_2 (out_3[1], in_1[1], in_2[1]);
  and and_3 (out_3[2], in_1[2], in_2[2]);
  and and_4 (out_3[3], in_1[3], in_2[3]);
  and and_5 (out_3[4], in_1[4], in_2[4]);
  and and_6 (out_3[5], in_1[5], in_2[5]);
  and and_7 (out_3[6], in_1[6], in_2[6]);
  and and_8 (out_3[7], in_1[7], in_2[7]);
  and and_9 (out_3[8], in_1[8], in_2[8]);
  and and_10 (out_3[9], in_1[9], in_2[9]);
  and and_11 (out_3[10], in_1[10], in_2[10]);
  and and_12 (out_3[11], in_1[11], in_2[11]);
  and and_13 (out_3[12], in_1[12], in_2[12]);
  and and_14 (out_3[13], in_1[13], in_2[13]);
  and and_15 (out_3[14], in_1[14], in_2[14]);
  and and_16 (out_3[15], in_1[15], in_2[15]);
endmodule

module mux (
  input  a,
  input  b,
  input  sel,
  output out
);

  wire and_1_out, and_2_out, not_1_out;

  not not_1 (not_1_out, sel);
  and and_1 (and_1_out, a, not_1_out);
  and and_2 (and_2_out, b, sel);
  or or_1 (out, and_1_out, and_2_out);

  // Notes on the sheet:
  //   if sel == 0 then out = a else out = b
endmodule

module mux4way (
  input  a,
  input  b,
  input  c,
  input  d,
  input  [1:0] sel,
  output out_6
);

  wire and_1_out, and_2_out, and_3_out, and_4_out, and_5_out, and_6_out, and_7_out, and_8_out, not_1_out,
       not_2_out, not_3_out, not_4_out, or_1_out, or_2_out;

  not not_1 (not_1_out, sel[0]);
  and and_1 (and_1_out, not_1_out, not_2_out);
  not not_2 (not_2_out, sel[1]);
  and and_2 (and_2_out, sel[0], not_3_out);
  not not_3 (not_3_out, sel[1]);
  not not_4 (not_4_out, sel[0]);
  and and_3 (and_3_out, not_4_out, sel[1]);
  and and_4 (and_4_out, sel[0], sel[1]);
  and and_5 (and_5_out, and_1_out, a);
  and and_6 (and_6_out, and_2_out, b);
  and and_7 (and_7_out, and_3_out, c);
  and and_8 (and_8_out, and_4_out, d);
  or or_1 (or_1_out, and_5_out, and_6_out);
  or or_2 (or_2_out, and_7_out, and_8_out);
  or or_3 (out_6, or_1_out, or_2_out);

  // Notes on the sheet:
  //   out = a if sel == 00 
  //   = b if sel == 01
  //   = c if sel == 10
  //   = d if sel == 11
endmodule

module dmux (
  input  in_1,
  input  sel,
  output out_3,
  output out_4
);

  wire not_1_out;

  and and_1 (out_3, in_1, not_1_out);
  not not_1 (not_1_out, sel);
  and and_2 (out_4, in_1, sel);
endmodule

module dmux4way (
  input  in_1,
  input  [1:0] sel,
  output out_3,
  output out_4,
  output out_5,
  output out_6
);

  wire and_1_out, and_2_out, and_3_out, and_4_out, not_1_out, not_2_out, not_3_out, not_4_out;

  not not_1 (not_1_out, sel[0]);
  not not_2 (not_2_out, sel[1]);
  not not_3 (not_3_out, sel[1]);
  not not_4 (not_4_out, sel[0]);
  and and_1 (and_1_out, not_1_out, not_2_out);
  and and_2 (and_2_out, sel[0], not_3_out);
  and and_3 (and_3_out, not_4_out, sel[1]);
  and and_4 (and_4_out, sel[0], sel[1]);
  and and_5 (out_3, and_1_out, in_1);
  and and_6 (out_4, and_2_out, in_1);
  and and_7 (out_5, and_3_out, in_1);
  and and_8 (out_6, and_4_out, in_1);
endmodule

module halfadder (
  input  a,
  input  b,
  output sum,
  output carry
);

  xor xor_1 (sum, a, b);
  and and_1 (carry, a, b);
endmodule

module fulladder (
  input  carry,
  input  a,
  input  b,
  output sum,
  output ca
);

  wire halfadder_1_carry, halfadder_1_sum, halfadder_2_carry;

  halfadder halfadder_1 (.a(a), .b(b), .sum(halfadder_1_sum), .carry(halfadder_1_carry));
  halfadder halfadder_2 (.a(carry), .b(halfadder_1_sum), .sum(sum), .carry(halfadder_2_carry));
  or or_1 (ca, halfadder_2_carry, halfadder_1_carry);
endmodule

module adder4 (
  input  in_1,
  input  [3:0] a,
  input  [3:0] b,
  output [3:0] sum,
  output carry
);

  wire fulladder_1_ca, fulladder_2_ca, fulladder_3_ca;

  fulladder fulladder_1 (.carry(in_1), .a(a[0]), .b(b[0]), .sum(sum[0]), .ca(fulladder_1_ca));
  fulladder fulladder_2 (.carry(fulladder_1_ca), .a(a[1]), .b(b[1]), .sum(sum[1]), .ca(fulladder_2_ca));
  fulladder fulladder_3 (.carry(fulladder_2_ca), .a(a[2]), .b(b[2]), .sum(sum[2]), .ca(fulladder_3_ca));
  fulladder fulladder_4 (.carry(fulladder_3_ca), .a(a[3]), .b(b[3]), .sum(sum[3]), .ca(carry));
endmodule

module adder8 (
  input  cin,
  input  [7:0] a,
  input  [7:0] b,
  output [7:0] sum,
  output cout
);

  wire adder4_1_carry;

  adder4 adder4_1 (.in_1(cin), .a(a[3:0]), .b(b[3:0]), .sum(sum[3:0]), .carry(adder4_1_carry));
  adder4 adder4_2 (.in_1(adder4_1_carry), .a(a[7:4]), .b(b[7:4]), .sum(sum[7:4]), .carry(cout));
endmodule

module adder16 (
  input  [15:0] a,
  input  [15:0] b,
  output [15:0] sum,
  output cout
);

  wire adder8_1_cout;

  adder8 adder8_1 (.cin(1'b0), .a(a[7:0]), .b(b[7:0]), .sum(sum[7:0]), .cout(adder8_1_cout));
  adder8 adder8_2 (.cin(adder8_1_cout), .a(a[15:8]), .b(b[15:8]), .sum(sum[15:8]), .cout(cout));
endmodule

module ALU (
  input  [15:0] x,
  input  zx,
  input  nx,
  input  [15:0] y,
  input  zy,
  input  ny,
  input  f,
  input  no,
  output [15:0] result,
  output zr,
  output ng
);

  wire or16way_1_out_2;
  wire [15:0] adder16_1_sum, and_1_out, multiplexer_1_out, multiplexer_2_out, multiplexer_3_out,
       multiplexer_4_out, multiplexer_5_out, not_1_out, not_2_out, not_3_out;

  Multiplexer #(.width(16)) multiplexer_1 (.in0(x), .in1({16{1'b0}}), .out(multiplexer_1_out), .sel(zx));
  Multiplexer #(.width(16)) multiplexer_2 (.in0(y), .in1({16{1'b0}}), .out(multiplexer_2_out), .sel(zy));
  assign not_1_out = ~multiplexer_1_out;  // NOT_Gate not_1, 16 bits wide
  assign not_2_out = ~multiplexer_2_out;  // NOT_Gate not_2, 16 bits wide
  Multiplexer #(.width(16)) multiplexer_3 (.in0(multiplexer_1_out), .in1(not_1_out), .out(multiplexer_3_out), .sel(nx));
  Multiplexer #(.width(16)) multiplexer_4 (.in0(multiplexer_2_out), .in1(not_2_out), .out(multiplexer_4_out), .sel(ny));
  assign and_1_out = multiplexer_3_out & multiplexer_4_out;  // AND_Gate and_1, 16 bits wide
  Multiplexer #(.width(16)) multiplexer_5 (.in0(and_1_out), .in1(adder16_1_sum), .out(multiplexer_5_out), .sel(f));
  adder16 adder16_1 (.a(multiplexer_3_out), .b(multiplexer_4_out), .sum(adder16_1_sum));  // open: cout
  assign not_3_out = ~multiplexer_5_out;  // NOT_Gate not_3, 16 bits wide
  Multiplexer #(.width(16)) multiplexer_6 (
    .in0(multiplexer_5_out), .in1(not_3_out), .out({ng, result[14:0]}), .sel(no));
  or16way or16way_1 (.in_1({ng, result[14:0]}), .out_2(or16way_1_out_2));
  not not_4 (zr, or16way_1_out_2);

  assign result[15] = ng;
endmodule

module Bit (
  input  load,
  input  a,
  input  clock,
  output result
);

  wire multiplexer_1_out;

  Multiplexer multiplexer_1 (.in0(result), .in1(a), .out(multiplexer_1_out), .sel(load));
  D_Flip_Flop d_ff_1 (.D(multiplexer_1_out), .clk(clock), .Q(result));  // open: Qn, preset, reset
endmodule

module Register8 (
  input  load,
  input  clock,
  input  [7:0] a,
  output [7:0] result
);

  Bit bit_1 (.load(load), .a(a[0]), .clock(clock), .result(result[0]));
  Bit bit_2 (.load(load), .a(a[1]), .clock(clock), .result(result[1]));
  Bit bit_3 (.load(load), .a(a[2]), .clock(clock), .result(result[2]));
  Bit bit_4 (.load(load), .a(a[3]), .clock(clock), .result(result[3]));
  Bit bit_5 (.load(load), .a(a[4]), .clock(clock), .result(result[4]));
  Bit bit_6 (.load(load), .a(a[5]), .clock(clock), .result(result[5]));
  Bit bit_7 (.load(load), .a(a[6]), .clock(clock), .result(result[6]));
  Bit bit_8 (.load(load), .a(a[7]), .clock(clock), .result(result[7]));
endmodule

module Register16 (
  input  load,
  input  clock,
  input  [15:0] a,
  output [15:0] result
);

  Register8 register8_1 (.load(load), .clock(clock), .a(a[7:0]), .result(result[7:0]));
  Register8 register8_2 (.load(load), .clock(clock), .a(a[15:8]), .result(result[15:8]));
endmodule

module SRAM8 (
  input  clock,
  input  [15:0] a,
  input  load,
  input  [2:0] address,
  output [15:0] result
);

  wire demultiplexer_1_out0, demultiplexer_1_out1, demultiplexer_1_out2, demultiplexer_1_out3,
       demultiplexer_1_out4, demultiplexer_1_out5, demultiplexer_1_out6, demultiplexer_1_out7;
  wire [15:0] register16_1_result, register16_2_result, register16_3_result, register16_4_result,
       register16_5_result, register16_6_result, register16_7_result, register16_8_result;

  Demultiplexer #(.select(3)) demultiplexer_1 (
    .out0(demultiplexer_1_out0), .out1(demultiplexer_1_out1), .out2(demultiplexer_1_out2),
    .out3(demultiplexer_1_out3), .out4(demultiplexer_1_out4), .out5(demultiplexer_1_out5),
    .out6(demultiplexer_1_out6), .out7(demultiplexer_1_out7), .in(load), .sel(address));
  Register16 register16_1 (.load(demultiplexer_1_out0), .clock(clock), .a(a), .result(register16_1_result));
  Register16 register16_2 (.load(demultiplexer_1_out1), .clock(clock), .a(a), .result(register16_2_result));
  Register16 register16_3 (.load(demultiplexer_1_out2), .clock(clock), .a(a), .result(register16_3_result));
  Register16 register16_4 (.load(demultiplexer_1_out3), .clock(clock), .a(a), .result(register16_4_result));
  Register16 register16_5 (.load(demultiplexer_1_out4), .clock(clock), .a(a), .result(register16_5_result));
  Register16 register16_6 (.load(demultiplexer_1_out5), .clock(clock), .a(a), .result(register16_6_result));
  Register16 register16_7 (.load(demultiplexer_1_out6), .clock(clock), .a(a), .result(register16_7_result));
  Register16 register16_8 (.load(demultiplexer_1_out7), .clock(clock), .a(a), .result(register16_8_result));
  Multiplexer #(.select(3), .width(16)) multiplexer_1 (
    .in0(register16_1_result), .in1(register16_2_result), .in2(register16_3_result),
    .in3(register16_4_result), .in4(register16_5_result), .in5(register16_6_result),
    .in6(register16_7_result), .in7(register16_8_result), .out(result), .sel(address));
endmodule

module SRAM64 (
  input  [15:0] a,
  input  clock,
  input  load,
  input  [5:0] address,
  output [15:0] result
);

  wire demultiplexer_1_out0, demultiplexer_1_out1, demultiplexer_1_out2, demultiplexer_1_out3,
       demultiplexer_1_out4, demultiplexer_1_out5, demultiplexer_1_out6, demultiplexer_1_out7;
  wire [15:0] sram8_1_result, sram8_2_result, sram8_3_result, sram8_4_result, sram8_5_result, sram8_6_result,
       sram8_7_result, sram8_8_result;

  Demultiplexer #(.select(3)) demultiplexer_1 (
    .out0(demultiplexer_1_out0), .out1(demultiplexer_1_out1), .out2(demultiplexer_1_out2),
    .out3(demultiplexer_1_out3), .out4(demultiplexer_1_out4), .out5(demultiplexer_1_out5),
    .out6(demultiplexer_1_out6), .out7(demultiplexer_1_out7), .in(load), .sel(address[5:3]));
  SRAM8 sram8_1 (.clock(clock), .a(a), .load(demultiplexer_1_out0), .address(address[2:0]), .result(sram8_1_result));
  SRAM8 sram8_2 (.clock(clock), .a(a), .load(demultiplexer_1_out1), .address(address[2:0]), .result(sram8_2_result));
  SRAM8 sram8_3 (.clock(clock), .a(a), .load(demultiplexer_1_out2), .address(address[2:0]), .result(sram8_3_result));
  SRAM8 sram8_4 (.clock(clock), .a(a), .load(demultiplexer_1_out3), .address(address[2:0]), .result(sram8_4_result));
  SRAM8 sram8_5 (.clock(clock), .a(a), .load(demultiplexer_1_out4), .address(address[2:0]), .result(sram8_5_result));
  SRAM8 sram8_6 (.clock(clock), .a(a), .load(demultiplexer_1_out5), .address(address[2:0]), .result(sram8_6_result));
  SRAM8 sram8_7 (.clock(clock), .a(a), .load(demultiplexer_1_out6), .address(address[2:0]), .result(sram8_7_result));
  SRAM8 sram8_8 (.clock(clock), .a(a), .load(demultiplexer_1_out7), .address(address[2:0]), .result(sram8_8_result));
  Multiplexer #(.select(3), .width(16)) multiplexer_1 (
    .in0(sram8_1_result), .in1(sram8_2_result), .in2(sram8_3_result), .in3(sram8_4_result),
    .in4(sram8_5_result), .in5(sram8_6_result), .in6(sram8_7_result), .in7(sram8_8_result), .out(result),
    .sel(address[5:3]));
endmodule

module Inc16 (
  input  [15:0] a,
  output [15:0] result,
  output carry
);

  adder16 adder16_1 (.a(a), .b(16'h1), .sum(result), .cout(carry));
endmodule

module CPU (
  input  [15:0] instruction,
  input  [15:0] inM,
  input  reset,
  input  clock,
  output [15:0] outM,
  output writeM,
  output [15:0] addressM,
  output [15:0] PC
);

  wire alu_1_ng, alu_1_zr, jumpchecker_1_jmp, multiplexer_2_out, mydecoder_1_f, mydecoder_1_isainstruction,
       mydecoder_1_no, mydecoder_1_nx, mydecoder_1_ny, mydecoder_1_writea, mydecoder_1_writed,
       mydecoder_1_zx, mydecoder_1_zy, not_1_out, not_2_out;
  wire [2:0] mydecoder_1_jump;
  wire [15:0] alu_1_result, DRegister_q, multiplexer_1_out, multiplexer_3_out, mydecoder_1_aregisterout,
       mydecoder_1_x, mydecoder_1_y;

  MyDecoder mydecoder_1 (
    .instruction(instruction), .DRegisterIn(DRegister_q), .ARegisterIn(addressM), .inM(inM),
    .ARegisterOut(mydecoder_1_aregisterout), .isAInstruction(mydecoder_1_isainstruction), .x(mydecoder_1_x),
    .y(mydecoder_1_y), .zx(mydecoder_1_zx), .nx(mydecoder_1_nx), .zy(mydecoder_1_zy), .ny(mydecoder_1_ny),
    .f(mydecoder_1_f), .no(mydecoder_1_no), .writeM(writeM), .writeD(mydecoder_1_writed),
    .writeA(mydecoder_1_writea), .jump(mydecoder_1_jump));
  Multiplexer #(.width(16)) multiplexer_1 (
    .in0(alu_1_result), .in1(mydecoder_1_aregisterout), .out(multiplexer_1_out),
    .sel(mydecoder_1_isainstruction));
  Multiplexer multiplexer_2 (
    .in0(mydecoder_1_writea), .in1(mydecoder_1_isainstruction), .out(multiplexer_2_out),
    .sel(mydecoder_1_isainstruction));
  Register #(.width(16)) ARegister (
    .D(multiplexer_1_out), .en(multiplexer_2_out), .clk(clock), .Q(addressM));  // open: clr
  Register #(.width(16)) DRegister (
    .D(alu_1_result), .en(mydecoder_1_writed), .clk(clock), .Q(DRegister_q));  // open: clr
  not not_1 (not_1_out, mydecoder_1_isainstruction);
  not not_2 (not_2_out, jumpchecker_1_jmp);
  ALU alu_1 (
    .x(mydecoder_1_x), .zx(mydecoder_1_zx), .nx(mydecoder_1_nx), .y(mydecoder_1_y), .zy(mydecoder_1_zy),
    .ny(mydecoder_1_ny), .f(mydecoder_1_f), .no(mydecoder_1_no), .result(alu_1_result), .zr(alu_1_zr),
    .ng(alu_1_ng));
  JumpChecker jumpchecker_1 (
    .zr(alu_1_zr), .ng(alu_1_ng), .jc(mydecoder_1_jump), .enable(not_1_out), .jmp(jumpchecker_1_jmp));
  PCRegister pcregister_1 (
    .a(multiplexer_3_out), .inc(not_2_out), .load(jumpchecker_1_jmp), .reset(reset), .clock(clock),
    .result(PC));
  Multiplexer #(.width(16)) multiplexer_3 (.in0(PC), .in1(addressM), .out(multiplexer_3_out), .sel(jumpchecker_1_jmp));
  Multiplexer #(.width(16)) multiplexer_4 (.in0({16{1'b0}}), .in1(alu_1_result), .out(outM), .sel(writeM));
endmodule

module PCRegister (
  input  [15:0] a,
  input  inc,
  input  load,
  input  reset,
  input  clock,
  output [15:0] result
);

  wire [15:0] inc16_1_result, multiplexer_1_out, multiplexer_2_out, multiplexer_3_out;

  Inc16 inc16_1 (.a(result), .result(inc16_1_result));  // open: carry
  Multiplexer #(.width(16)) multiplexer_1 (.in0(result), .in1(inc16_1_result), .out(multiplexer_1_out), .sel(inc));
  Multiplexer #(.width(16)) multiplexer_2 (.in0(multiplexer_1_out), .in1(a), .out(multiplexer_2_out), .sel(load));
  Multiplexer #(.width(16)) multiplexer_3 (
    .in0(multiplexer_2_out), .in1({16{1'b0}}), .out(multiplexer_3_out), .sel(reset));
  Register #(.width(16)) register_1 (.D(multiplexer_3_out), .en(1'b1), .clk(clock), .Q(result));  // open: clr
endmodule

module MyDecoder (
  input  [15:0] instruction,
  input  [15:0] DRegisterIn,
  input  [15:0] ARegisterIn,
  input  [15:0] inM,
  output [15:0] ARegisterOut,
  output isAInstruction,
  output [15:0] x,
  output [15:0] y,
  output zx,
  output nx,
  output zy,
  output ny,
  output f,
  output no,
  output writeM,
  output writeD,
  output writeA,
  output [2:0] jump
);

  not not_1 (isAInstruction, instruction[15]);
  Multiplexer #(.width(16)) multiplexer_1 (.in0(ARegisterIn), .in1(inM), .out(y), .sel(instruction[12]));
  Multiplexer multiplexer_2 (.in0(1'b0), .in1(instruction[3]), .out(writeM), .sel(instruction[15]));
  Multiplexer multiplexer_3 (.in0(1'b0), .in1(instruction[4]), .out(writeD), .sel(instruction[15]));
  Multiplexer multiplexer_4 (.in0(1'b0), .in1(instruction[5]), .out(writeA), .sel(instruction[15]));

  assign ARegisterOut = {1'b0, instruction[14:0]};
  assign f = instruction[7];
  assign jump = instruction[2:0];
  assign no = instruction[6];
  assign nx = instruction[10];
  assign ny = instruction[8];
  assign x = DRegisterIn;
  assign zx = instruction[11];
  assign zy = instruction[9];
endmodule

module JumpChecker (
  input  zr,
  input  ng,
  input  [2:0] jc,
  input  enable,
  output jmp
);

  wire and_1_out, multiplexer_1_out, not_1_out, not_2_out, not_3_out, or_1_out;

  not not_1 (not_1_out, zr);
  not not_2 (not_2_out, ng);
  not not_3 (not_3_out, 1'b0);
  and and_1 (and_1_out, not_1_out, not_2_out);
  or or_1 (or_1_out, zr, ng);
  Multiplexer #(.select(3)) multiplexer_1 (
    .in0(1'b0), .in1(and_1_out), .in2(zr), .in3(not_2_out), .in4(ng), .in5(not_1_out), .in6(or_1_out),
    .in7(not_3_out), .out(multiplexer_1_out), .sel(jc));
  and and_2 (jmp, multiplexer_1_out, enable);
endmodule

module TestInstructions (
  input  in_1,
  output [15:0] out_2,
  output [15:0] out_3,
  output [15:0] out_4,
  output [15:0] out_5
);

  wire and_1_out, and_2_out, and_3_out, clock_1_out, cpu_1_writem, not_1_out, not_2_out;
  wire [12:0] multiplexer_1_out;
  wire [15:0] controlled_buffer_1_out, cpu_1_outm, ram_2_dout;

  ROM #(.addrWidth(16), .dataWidth(16)) rom_1 (.addr(out_4), .data(out_2));
  Clock clock_1 (.out(clock_1_out));
  CPU cpu_1 (
    .instruction(out_2), .inM(out_3), .reset(in_1), .clock(clock_1_out), .outM(cpu_1_outm),
    .writeM(cpu_1_writem), .addressM(out_5), .PC(out_4));
  not not_1 (not_1_out, cpu_1_writem);
  not not_2 (not_2_out, out_5[14]);
  and and_1 (and_1_out, cpu_1_writem, not_2_out);
  and and_2 (and_2_out, not_1_out, not_2_out);
  assign controlled_buffer_1_out = and_1_out ? cpu_1_outm : 16'bz;  // Controlled_Buffer controlled_buffer_1
  and and_3 (and_3_out, cpu_1_writem, out_5[14]);
  Multiplexer #(.width(13)) multiplexer_1 (
    .in0({13{1'b0}}), .in1(out_5[12:0]), .out(multiplexer_1_out), .sel(out_5[14]));
  RAM #(.addrWidth(14), .dataWidth(16)) ram_1 (
    .addr(out_5[13:0]), .we(and_1_out), .oe(and_2_out), .clk(clock_1_out), .din(controlled_buffer_1_out),
    .dout(out_3));
  RAM #(.addrWidth(13), .dataWidth(16)) ram_2 (
    .addr(multiplexer_1_out), .we(and_3_out), .oe(not_2_out), .clk(clock_1_out), .din(cpu_1_outm),
    .dout(ram_2_dout));
  Hex_Digit_Display hex_digit_display_1 (.value(ram_2_dout[15:12]));  // open: dp
  Hex_Digit_Display hex_digit_display_2 (.value(ram_2_dout[11:8]));  // open: dp
  Hex_Digit_Display hex_digit_display_3 (.value(ram_2_dout[7:4]));  // open: dp
  Hex_Digit_Display hex_digit_display_4 (.value(ram_2_dout[3:0]));  // open: dp

  // Notes on the sheet:
  //   contents of rom_1 (hex, n*v repeats v):
  //   ea80 ea90 e7d0 0 ea80 e308 4000 ea80 e308 2 ea87
endmodule

module TestRAM (
  input  [7:0] address,
  input  load,
  input  clock,
  input  [7:0] in_4,
  output [7:0] out_5
);

  wire not_1_out;
  wire [7:0] controlled_buffer_1_out;

  not not_1 (not_1_out, load);
  assign controlled_buffer_1_out = not_1_out ? in_4 : 8'bz;  // Controlled_Buffer controlled_buffer_1
  RAM ram_1 (.addr(address), .we(not_1_out), .oe(load), .clk(clock), .din(controlled_buffer_1_out), .dout(out_5));
endmodule

module TestHexDigitDisplay (
  input  [3:0] in_1,
  input  [63:0] in_2
);

  Hex_Digit_Display hex_digit_display_1 (.value(in_1));  // open: dp
  DotMatrix #(.matrixcols(64), .matrixrows(64)) dotmatrix_1 (.col0(in_2));  // open: col1, col2, col3, col4, col5, col6, col7, col8, col9, col10, col11, col12, col13, col14, col15, col16, col17, col18, col19, col20, col21, col22, col23, col24, col25, col26, col27, col28, col29, col30, col31, col32, col33, col34, col35, col36, col37, col38, col39, col40, col41, col42, col43, col44, col45, col46, col47, col48, col49, col50, col51, col52, col53, col54, col55, col56, col57, col58, col59, col60, col61, col62, col63
endmodule

module VedioController (
  input  clock,
  input  [15:0] data,
  input  [15:0] address,
  input  we,
  output [9:0] oaddr,
  output write,
  output read,
  output [15:0] odata
);

  wire not_1_out, not_2_out;
  wire [1:0] register_1_q, register_1_q_2, register_1_q_3;
  wire [15:0] adder16_1_sum, multiplexer_1_out, undriven_2;
  wire [15:10] multiplexer_2_out, undriven;

  not not_1 (not_1_out, address[10]);
  not not_2 (not_2_out, address[15]);
  and and_1 (write, not_1_out, address[14], not_2_out, we);
  adder16 adder16_1 (.a(undriven_2), .b(16'h1), .sum(adder16_1_sum));  // open: cout
  Multiplexer #(.width(16)) multiplexer_1 (.in0(adder16_1_sum), .in1(undriven_2), .out(multiplexer_1_out), .sel(write));
  Register #(.width(16)) register_1 (
    .D(multiplexer_1_out), .en(1'b1), .clk(clock),
    .Q({register_1_q_3, register_1_q_2, register_1_q, undriven_2[9:0]}));  // open: clr
  Multiplexer #(.width(16)) multiplexer_2 (
    .in0({register_1_q_3, register_1_q_2, register_1_q, undriven_2[9:0]}), .in1({undriven, address[9:0]}),
    .out({multiplexer_2_out, oaddr}), .sel(write));
  not not_3 (read, write);

  assign odata = data;
endmodule

module ColBuffer (
  input  [9:0] address,
  input  [15:0] data,
  input  clock,
  output [15:0] odata,
  output we,
  output [5:0] oaddr
);

  wire demultiplexer_1_out1, demultiplexer_1_out2, demultiplexer_1_out3, demultiplexer_1_out4,
       demultiplexer_1_out5, demultiplexer_1_out6, demultiplexer_1_out7, demultiplexer_1_out8,
       demultiplexer_1_out9, demultiplexer_1_out10, demultiplexer_1_out11, demultiplexer_1_out12,
       demultiplexer_1_out13, demultiplexer_1_out14, demultiplexer_1_out15;
  wire [1:0] undriven;
  wire [7:6] adder8_1_sum;

  Demultiplexer #(.select(4)) demultiplexer_1 (
    .out0(we), .out1(demultiplexer_1_out1), .out2(demultiplexer_1_out2), .out3(demultiplexer_1_out3),
    .out4(demultiplexer_1_out4), .out5(demultiplexer_1_out5), .out6(demultiplexer_1_out6),
    .out7(demultiplexer_1_out7), .out8(demultiplexer_1_out8), .out9(demultiplexer_1_out9),
    .out10(demultiplexer_1_out10), .out11(demultiplexer_1_out11), .out12(demultiplexer_1_out12),
    .out13(demultiplexer_1_out13), .out14(demultiplexer_1_out14), .out15(demultiplexer_1_out15), .in(1'b1),
    .sel(address[3:0]));
  Register #(.width(1)) register_1 (.D(data[0]), .en(we), .clk(clock), .Q(odata[0]));  // open: clr
  Register #(.width(1)) register_2 (.D(data[0]), .en(demultiplexer_1_out4), .clk(clock), .Q(odata[4]));  // open: clr
  Register #(.width(1)) register_3 (.D(data[0]), .en(demultiplexer_1_out8), .clk(clock), .Q(odata[8]));  // open: clr
  Register #(.width(1)) register_4 (.D(data[0]), .en(demultiplexer_1_out12), .clk(clock), .Q(odata[12]));  // open: clr
  adder8 adder8_1 (.cin(1'b0), .a({undriven, address[9:4]}), .b({8{1'b1}}), .sum({adder8_1_sum, oaddr}));  // open: cout
  Register #(.width(1)) register_5 (.D(data[0]), .en(demultiplexer_1_out1), .clk(clock), .Q(odata[1]));  // open: clr
  Register #(.width(1)) register_6 (.D(data[0]), .en(demultiplexer_1_out5), .clk(clock), .Q(odata[5]));  // open: clr
  Register #(.width(1)) register_7 (.D(data[0]), .en(demultiplexer_1_out9), .clk(clock), .Q(odata[9]));  // open: clr
  Register #(.width(1)) register_8 (.D(data[0]), .en(demultiplexer_1_out13), .clk(clock), .Q(odata[13]));  // open: clr
  Register #(.width(1)) register_9 (.D(data[0]), .en(demultiplexer_1_out2), .clk(clock), .Q(odata[2]));  // open: clr
  Register #(.width(1)) register_10 (.D(data[0]), .en(demultiplexer_1_out6), .clk(clock), .Q(odata[6]));  // open: clr
  Register #(.width(1)) register_11 (.D(data[0]), .en(demultiplexer_1_out10), .clk(clock), .Q(odata[10]));  // open: clr
  Register #(.width(1)) register_12 (.D(data[0]), .en(demultiplexer_1_out14), .clk(clock), .Q(odata[14]));  // open: clr
  Register #(.width(1)) register_13 (.D(data[0]), .en(demultiplexer_1_out3), .clk(clock), .Q(odata[3]));  // open: clr
  Register #(.width(1)) register_14 (.D(data[0]), .en(demultiplexer_1_out7), .clk(clock), .Q(odata[7]));  // open: clr
  Register #(.width(1)) register_15 (.D(data[0]), .en(demultiplexer_1_out11), .clk(clock), .Q(odata[11]));  // open: clr
  Register #(.width(1)) register_16 (.D(data[0]), .en(demultiplexer_1_out15), .clk(clock), .Q(odata[15]));  // open: clr
endmodule

module VedioDecoder (
  input  clock,
  input  [15:0] data,
  input  we,
  input  [15:0] address,
  output [31:0] osig0,
  output [31:0] osig1,
  output [31:0] osig2,
  output [31:0] osig3,
  output [31:0] osig4,
  output [31:0] osig5,
  output [31:0] osig6,
  output [31:0] osig7,
  output [31:0] osig8,
  output [31:0] osig9,
  output [31:0] osig10,
  output [31:0] osig11,
  output [31:0] osig12,
  output [31:0] osig13,
  output [31:0] osig14,
  output [31:0] osig15,
  output [31:0] osig16,
  output [31:0] osig17,
  output [31:0] osig18,
  output [31:0] osig19,
  output [31:0] osig20,
  output [31:0] osig21,
  output [31:0] osig22,
  output [31:0] osig23,
  output [31:0] osig24,
  output [31:0] osig25,
  output [31:0] osig26,
  output [31:0] osig27,
  output [31:0] osig28,
  output [31:0] osig29,
  output [31:0] osig30,
  output [31:0] osig31
);

  wire and_1_out, and_2_out, demultiplexer_1_out0, demultiplexer_1_out1, demultiplexer_1_out2,
       demultiplexer_1_out3, demultiplexer_1_out4, demultiplexer_1_out5, demultiplexer_1_out6,
       demultiplexer_1_out7, not_1_out, not_2_out;

  and and_1 (and_1_out, we, and_2_out);
  not not_1 (not_1_out, address[10]);
  not not_2 (not_2_out, address[15]);
  Demultiplexer #(.select(3)) demultiplexer_1 (
    .out0(demultiplexer_1_out0), .out1(demultiplexer_1_out1), .out2(demultiplexer_1_out2),
    .out3(demultiplexer_1_out3), .out4(demultiplexer_1_out4), .out5(demultiplexer_1_out5),
    .out6(demultiplexer_1_out6), .out7(demultiplexer_1_out7), .in(and_1_out), .sel(address[9:7]));
  and and_2 (and_2_out, not_1_out, address[14], not_2_out);
  VedioBuffer4 vediobuffer4_1 (
    .write(demultiplexer_1_out0), .data(data[0]), .clock(clock), .address(address[6:0]), .osig0(osig0),
    .osig1(osig1), .osig2(osig2), .osig3(osig3));
  VedioBuffer4 vediobuffer4_2 (
    .write(demultiplexer_1_out2), .data(data[0]), .clock(clock), .address(address[6:0]), .osig0(osig8),
    .osig1(osig9), .osig2(osig10), .osig3(osig11));
  VedioBuffer4 vediobuffer4_3 (
    .write(demultiplexer_1_out4), .data(data[0]), .clock(clock), .address(address[6:0]), .osig0(osig16),
    .osig1(osig17), .osig2(osig18), .osig3(osig19));
  VedioBuffer4 vediobuffer4_4 (
    .write(demultiplexer_1_out6), .data(data[0]), .clock(clock), .address(address[6:0]), .osig0(osig24),
    .osig1(osig25), .osig2(osig26), .osig3(osig27));
  VedioBuffer4 vediobuffer4_5 (
    .write(demultiplexer_1_out1), .data(data[0]), .clock(clock), .address(address[6:0]), .osig0(osig4),
    .osig1(osig5), .osig2(osig6), .osig3(osig7));
  VedioBuffer4 vediobuffer4_6 (
    .write(demultiplexer_1_out3), .data(data[0]), .clock(clock), .address(address[6:0]), .osig0(osig12),
    .osig1(osig13), .osig2(osig14), .osig3(osig15));
  VedioBuffer4 vediobuffer4_7 (
    .write(demultiplexer_1_out5), .data(data[0]), .clock(clock), .address(address[6:0]), .osig0(osig20),
    .osig1(osig21), .osig2(osig22), .osig3(osig23));
  VedioBuffer4 vediobuffer4_8 (
    .write(demultiplexer_1_out7), .data(data[0]), .clock(clock), .address(address[6:0]), .osig0(osig28),
    .osig1(osig29), .osig2(osig30), .osig3(osig31));
endmodule

module VedioBuffer4 (
  input  write,
  input  data,
  input  clock,
  input  [6:0] address,
  output [31:0] osig0,
  output [31:0] osig1,
  output [31:0] osig2,
  output [31:0] osig3
);

  wire demultiplexer_1_out0, demultiplexer_1_out1, demultiplexer_1_out2, demultiplexer_1_out3;

  Demultiplexer #(.select(2)) demultiplexer_1 (
    .out0(demultiplexer_1_out0), .out1(demultiplexer_1_out1), .out2(demultiplexer_1_out2),
    .out3(demultiplexer_1_out3), .in(write), .sel(address[6:5]));
  VedioCol vediocol_1 (.clock(clock), .data(data), .we(demultiplexer_1_out0), .address(address[4:0]), .osig(osig0));
  VedioCol vediocol_2 (.clock(clock), .data(data), .we(demultiplexer_1_out1), .address(address[4:0]), .osig(osig1));
  VedioCol vediocol_3 (.clock(clock), .data(data), .we(demultiplexer_1_out2), .address(address[4:0]), .osig(osig2));
  VedioCol vediocol_4 (.clock(clock), .data(data), .we(demultiplexer_1_out3), .address(address[4:0]), .osig(osig3));
endmodule

module Pixel8 (
  input  we,
  input  [2:0] address,
  input  clock,
  input  data,
  output [7:0] out_5
);

  wire demultiplexer_1_out0, demultiplexer_1_out1, demultiplexer_1_out2, demultiplexer_1_out3,
       demultiplexer_1_out4, demultiplexer_1_out5, demultiplexer_1_out6, demultiplexer_1_out7;

  Demultiplexer #(.select(3)) demultiplexer_1 (
    .out0(demultiplexer_1_out0), .out1(demultiplexer_1_out1), .out2(demultiplexer_1_out2),
    .out3(demultiplexer_1_out3), .out4(demultiplexer_1_out4), .out5(demultiplexer_1_out5),
    .out6(demultiplexer_1_out6), .out7(demultiplexer_1_out7), .in(we), .sel(address));
  Register #(.width(1)) register_1 (.D(data), .en(demultiplexer_1_out0), .clk(clock), .Q(out_5[0]));  // open: clr
  Register #(.width(1)) register_2 (.D(data), .en(demultiplexer_1_out2), .clk(clock), .Q(out_5[2]));  // open: clr
  Register #(.width(1)) register_3 (.D(data), .en(demultiplexer_1_out4), .clk(clock), .Q(out_5[4]));  // open: clr
  Register #(.width(1)) register_4 (.D(data), .en(demultiplexer_1_out6), .clk(clock), .Q(out_5[6]));  // open: clr
  Register #(.width(1)) register_5 (.D(data), .en(demultiplexer_1_out1), .clk(clock), .Q(out_5[1]));  // open: clr
  Register #(.width(1)) register_6 (.D(data), .en(demultiplexer_1_out3), .clk(clock), .Q(out_5[3]));  // open: clr
  Register #(.width(1)) register_7 (.D(data), .en(demultiplexer_1_out5), .clk(clock), .Q(out_5[5]));  // open: clr
  Register #(.width(1)) register_8 (.D(data), .en(demultiplexer_1_out7), .clk(clock), .Q(out_5[7]));  // open: clr
endmodule

module VedioCol (
  input  clock,
  input  data,
  input  we,
  input  [4:0] address,
  output [31:0] osig
);

  wire demultiplexer_1_out0, demultiplexer_1_out1, demultiplexer_1_out2, demultiplexer_1_out3;

  Demultiplexer #(.select(2)) demultiplexer_1 (
    .out0(demultiplexer_1_out0), .out1(demultiplexer_1_out1), .out2(demultiplexer_1_out2),
    .out3(demultiplexer_1_out3), .in(we), .sel(address[4:3]));
  Pixel8 pixel8_1 (.we(demultiplexer_1_out0), .address(address[2:0]), .clock(clock), .data(data), .out_5(osig[7:0]));
  Pixel8 pixel8_2 (.we(demultiplexer_1_out1), .address(address[2:0]), .clock(clock), .data(data), .out_5(osig[15:8]));
  Pixel8 pixel8_3 (.we(demultiplexer_1_out2), .address(address[2:0]), .clock(clock), .data(data), .out_5(osig[23:16]));
  Pixel8 pixel8_4 (.we(demultiplexer_1_out3), .address(address[2:0]), .clock(clock), .data(data), .out_5(osig[31:24]));
endmodule

module HackComputer (
  input  in_1,
  output [15:0] out_2,
  output [15:0] out_3,
  output [15:0] out_4,
  output [15:0] out_5
);

  wire and_1_out, and_2_out, and_3_out, clock_1_out, clock_2_out, cpu_1_writem, keyboard_1_avail, not_1_out,
       not_2_out, not_3_out, register_1_q;
  wire [6:0] keyboard_1_data;
  wire [15:0] controlled_buffer_1_out, cpu_1_outm, multiplexer_1_out, register_2_q;
  wire [15:7] undriven;
  wire [31:0] vediodecoder_1_osig0, vediodecoder_1_osig1, vediodecoder_1_osig2, vediodecoder_1_osig3,
       vediodecoder_1_osig4, vediodecoder_1_osig5, vediodecoder_1_osig6, vediodecoder_1_osig7,
       vediodecoder_1_osig8, vediodecoder_1_osig9, vediodecoder_1_osig10, vediodecoder_1_osig11,
       vediodecoder_1_osig12, vediodecoder_1_osig13, vediodecoder_1_osig14, vediodecoder_1_osig15,
       vediodecoder_1_osig16, vediodecoder_1_osig17, vediodecoder_1_osig18, vediodecoder_1_osig19,
       vediodecoder_1_osig20, vediodecoder_1_osig21, vediodecoder_1_osig22, vediodecoder_1_osig23,
       vediodecoder_1_osig24, vediodecoder_1_osig25, vediodecoder_1_osig26, vediodecoder_1_osig27,
       vediodecoder_1_osig28, vediodecoder_1_osig29, vediodecoder_1_osig30, vediodecoder_1_osig31;

  ROM #(.addrWidth(16), .dataWidth(16)) rom_1 (.addr(out_4), .data(out_2));
  Clock clock_1 (.out(clock_1_out));
  Clock clock_2 (.out(clock_2_out));
  Keyboard keyboard_1 (.clk(clock_2_out), .avail(keyboard_1_avail), .data(keyboard_1_data));  // open: re, clr
  not not_1 (not_1_out, out_5[15]);
  Multiplexer #(.width(16)) multiplexer_1 (
    .in0(out_3), .in1(register_2_q), .out(multiplexer_1_out), .sel(register_1_q));
  CPU cpu_1 (
    .instruction(out_2), .inM(multiplexer_1_out), .reset(in_1), .clock(clock_1_out), .outM(cpu_1_outm),
    .writeM(cpu_1_writem), .addressM(out_5), .PC(out_4));
  Register #(.width(1)) register_1 (.D(and_1_out), .en(1'b1), .clk(clock_1_out), .Q(register_1_q));  // open: clr
  and and_1 (and_1_out, out_5[10], not_1_out, out_5[14]);
  not not_2 (not_2_out, cpu_1_writem);
  not not_3 (not_3_out, out_5[14]);
  and and_2 (and_2_out, cpu_1_writem, not_3_out);
  and and_3 (and_3_out, not_2_out, not_3_out);
  assign controlled_buffer_1_out = and_2_out ? cpu_1_outm : 16'bz;  // Controlled_Buffer controlled_buffer_1
  RAM #(.addrWidth(14), .dataWidth(16)) ram_1 (
    .addr(out_5[13:0]), .we(and_2_out), .oe(and_3_out), .clk(clock_1_out), .din(controlled_buffer_1_out),
    .dout(out_3));
  Register #(.width(16)) register_2 (
    .D({undriven, keyboard_1_data}), .en(keyboard_1_avail), .clk(clock_2_out), .Q(register_2_q));  // open: clr
  DotMatrix #(.matrixcols(32), .matrixrows(32)) dotmatrix_1 (
    .col0(vediodecoder_1_osig0), .col1(vediodecoder_1_osig1), .col2(vediodecoder_1_osig2),
    .col3(vediodecoder_1_osig3), .col4(vediodecoder_1_osig4), .col5(vediodecoder_1_osig5),
    .col6(vediodecoder_1_osig6), .col7(vediodecoder_1_osig7), .col8(vediodecoder_1_osig8),
    .col9(vediodecoder_1_osig9), .col10(vediodecoder_1_osig10), .col11(vediodecoder_1_osig11),
    .col12(vediodecoder_1_osig12), .col13(vediodecoder_1_osig13), .col14(vediodecoder_1_osig14),
    .col15(vediodecoder_1_osig15), .col16(vediodecoder_1_osig16), .col17(vediodecoder_1_osig17),
    .col18(vediodecoder_1_osig18), .col19(vediodecoder_1_osig19), .col20(vediodecoder_1_osig20),
    .col21(vediodecoder_1_osig21), .col22(vediodecoder_1_osig22), .col23(vediodecoder_1_osig23),
    .col24(vediodecoder_1_osig24), .col25(vediodecoder_1_osig25), .col26(vediodecoder_1_osig26),
    .col27(vediodecoder_1_osig27), .col28(vediodecoder_1_osig28), .col29(vediodecoder_1_osig29),
    .col30(vediodecoder_1_osig30), .col31(vediodecoder_1_osig31));
  VedioDecoder vediodecoder_1 (
    .clock(clock_1_out), .data(cpu_1_outm), .we(cpu_1_writem), .address(out_5), .osig0(vediodecoder_1_osig0),
    .osig1(vediodecoder_1_osig1), .osig2(vediodecoder_1_osig2), .osig3(vediodecoder_1_osig3),
    .osig4(vediodecoder_1_osig4), .osig5(vediodecoder_1_osig5), .osig6(vediodecoder_1_osig6),
    .osig7(vediodecoder_1_osig7), .osig8(vediodecoder_1_osig8), .osig9(vediodecoder_1_osig9),
    .osig10(vediodecoder_1_osig10), .osig11(vediodecoder_1_osig11), .osig12(vediodecoder_1_osig12),
    .osig13(vediodecoder_1_osig13), .osig14(vediodecoder_1_osig14), .osig15(vediodecoder_1_osig15),
    .osig16(vediodecoder_1_osig16), .osig17(vediodecoder_1_osig17), .osig18(vediodecoder_1_osig18),
    .osig19(vediodecoder_1_osig19), .osig20(vediodecoder_1_osig20), .osig21(vediodecoder_1_osig21),
    .osig22(vediodecoder_1_osig22), .osig23(vediodecoder_1_osig23), .osig24(vediodecoder_1_osig24),
    .osig25(vediodecoder_1_osig25), .osig26(vediodecoder_1_osig26), .osig27(vediodecoder_1_osig27),
    .osig28(vediodecoder_1_osig28), .osig29(vediodecoder_1_osig29), .osig30(vediodecoder_1_osig30),
    .osig31(vediodecoder_1_osig31));

  // Notes on the sheet:
  //   contents of rom_1 (hex, n*v repeats v):
  //   ea80 4000 ec10 0 ea80 e308 0 ea80 fc10 e320 ea80 efc8 e7d0 0 ea80 e308 4400 e1d0 6 e301 1 ea87
endmodule
